# Fritzing sketch session2LastPart (saved by Fritzing 0.9.4)
breadboards: 1

parts:
  U1 = 74HC04_HEX_INVERTER [package=dil14]
  U2 = 74HC04_HEX_INVERTER [package=dil14]

nets:
  N1: U1.1Y, U1.2A
  N2: U1.2Y, U1.3A
  N3: U1.3Y, U1.6A
  N4: U1.4Y, U2.1A
  N5: U1.4A, U1.5Y
  N6: U1.5A, U1.6Y
  N7: U2.1Y, U2.2A
  N8: U2.2Y, U2.3A
  N9: U2.3Y, U2.6A
  N10: U2.4A, U2.5Y
  N11: U2.5A, U2.6Y
