# Fritzing sketch exp4 (saved by Fritzing 0.9.4)
breadboards: 1

parts:
  U1 = 74HC595 [package="DIP16 [THT]"]
  U2 = 74HC04_HEX_INVERTER [package=dil14]

nets:
  GND: U1.GND, U2.GND
  N1: U1.Q7', U2.1A
  N2: U1.DS, U2.1Y
  VCC: U1.VCC, U2.VCC

notes:
  clock
  output
