# Fritzing sketch session2 (saved by Fritzing 0.9.4)
breadboards: 1

parts:
  U1 = 555 Timer [package="SO8 [SMD]"]
  C1 = Electrolytic Capacitor [capacitance=1µF package="100 mil [THT, electrolytic]"]
  R1_14k = Resistor [tolerance=±5% resistance=220 package=THT]
  R1 = Resistor [tolerance=±5% resistance=220 package=THT]
  C2 = Electrolytic Capacitor [capacitance=1µF package="100 mil [THT, electrolytic]"]  # not connected

nets:
  N1: U1.Pin_4, R1.Pin_1
  N2: C1.-, R1_14k.Pin_0
  N3: R1_14k.Pin_1, R1.Pin_0
